# Fritzing sketch bomb2.1 (saved by Fritzing 0.9.3b)

parts:
  LCM1602_IIC1 = LCM1602 IIC [part_number="LCM1602 IIC" chip_label="LCM1602 IIC" package="DIP (Dual Inline) [THT]"]
  Part1 = Arduino Mega 2560 (Rev3)
  Matrix_keypad1 = KEYPAD 4x4
  SP1 = SPEAKER [package=pcb_mount_speaker]
  SHIFT1 = TPIC6B595
  SHIFT2 = TPIC6B595
  Power_plug1 = Power plug
  IC1 = V_REG_LD1117VXX [package=78xxl]
  R1 = Resistor [tolerance=±5% resistance=10k package=THT]
  R2 = Resistor [tolerance=±5% resistance=10k package=THT]

nets:
  GND: LCM1602_IIC1.GND, Part1.GND, SP1.+
  VCC: LCM1602_IIC1.VCC, Part1.5V
  N1: LCM1602_IIC1.SDA, Part1.D20/SDA, Part1.SDA
  N2: LCM1602_IIC1.SCL, Part1.SCL
  N3: Part1.A8, Matrix_keypad1.col1
  N4: Part1.A9, Matrix_keypad1.col2
  N5: Part1.A10, Matrix_keypad1.col3
  N6: Part1.A11, Matrix_keypad1.col4
  N7: Part1.A12, Matrix_keypad1.row1
  N8: Part1.A13, Matrix_keypad1.row2
  N9: Part1.A14, Matrix_keypad1.row3
  N10: Part1.A15, Matrix_keypad1.row4
  N11: Part1.D9_PWM, SP1.-
  N12: Part1.D26, SHIFT2.SER_IN
  N13: Part1.D28, SHIFT1.RCK, SHIFT2.RCK
  N14: Part1.D30, SHIFT1.SRCK, SHIFT2.SRCK
  N15: SHIFT1.SER_IN, SHIFT2.SER_OUT
  N16: SHIFT1.SRCLR, R1.Pin_1
  GND_2: SHIFT1.G, SHIFT1.GND, SHIFT2.G, SHIFT2.GND, Power_plug1.GND, IC1.GND
  VCC_2: SHIFT1.VCC, SHIFT2.VCC, IC1.OUT, R1.Pin_0, R2.Pin_0
  N17: SHIFT2.SRCLR, R2.Pin_1
  N18: Power_plug1.VCC, IC1.IN

custom parts:
  LCM1602 IIC: I2C-Module to use a 1602 or 2004 LCD on with the wire.h libory Serial LCD Modul
  KEYPAD 4x4: Matrix keypad 16 buttons, 4 rows x 4 columns
  TPIC6B595: 8-bit high-power parallel-load shift register
